// Logisim project processor-mul.circ as structural Verilog
module ALU (
  input  [2:0] F,
  input  [31:0] B,
  input  [31:0] A,
  output [31:0] Y,
  output Zero
);

  wire and_4_out, bitselector_1_out;
  wire [31:0] adder_1_out, and_1_out, and_2_out, and_3_out, bit_extender_1_out, multiplexer_1_out,
       multiplexer_2_out, multiplier_1_out, nor_1_out, not_1_out, not_2_out, not_3_out, or_1_out, undriven,
       undriven_2;

  assign not_1_out = ~B;  // NOT_Gate not_1, 32 bits wide
  Multiplexer #(.width(32)) multiplexer_1 (.in0(B), .in1(not_1_out), .out(multiplexer_1_out), .sel(F[2]));  // open: en
  Multiplier #(.width(32)) multiplier_1 (.a(multiplexer_1_out), .b(A), .out(multiplier_1_out));  // open: cin, cout
  Adder #(.width(32)) adder_1 (.a(multiplexer_1_out), .b(A), .out(adder_1_out), .cin(F[2]));  // open: cout
  assign and_1_out = multiplexer_1_out & A;  // AND_Gate and_1, 32 bits wide
  assign or_1_out = multiplexer_1_out | A;  // OR_Gate or_1, 32 bits wide
  Multiplexer #(.width(32)) multiplexer_2 (
    .in0(multiplier_1_out), .in1({{31{1'b0}}, adder_1_out[31]}), .out(multiplexer_2_out), .sel(F[2]));  // open: en
  Multiplexer #(.select(2), .width(32)) multiplexer_3 (
    .in0(and_1_out), .in1(or_1_out), .in2(adder_1_out), .in3(multiplexer_2_out), .out(Y), .sel(F[1:0]));  // open: en
  Comparator #(.width(32), .mode("unsigned")) comparator_1 (.a(Y), .b({32{1'b0}}), .eq(Zero));  // open: gt, lt
  assign not_2_out = ~undriven_2;  // NOT_Gate not_2, 32 bits wide
  assign not_3_out = ~{32{1'b0}};  // NOT_Gate not_3, 32 bits wide
  BitSelector #(.width(32)) bitselector_1 (.in(undriven), .out(bitselector_1_out), .sel({5{1'b1}}));
  assign and_2_out = not_2_out & {32{1'b0}};  // AND_Gate and_2, 32 bits wide
  assign and_3_out = undriven_2 & not_3_out;  // AND_Gate and_3, 32 bits wide
  assign bit_extender_1_out = {{31{1'b0}}, bitselector_1_out};  // Bit_Extender bit_extender_1
  assign nor_1_out = ~(and_2_out | and_3_out);  // NOR_Gate nor_1, 32 bits wide
  and and_4 (and_4_out, nor_1_out[0], nor_1_out[1], nor_1_out[2], nor_1_out[3], nor_1_out[4], nor_1_out[5], nor_1_out[6], nor_1_out[7], nor_1_out[8], nor_1_out[9], nor_1_out[10], nor_1_out[11], nor_1_out[12], nor_1_out[13], nor_1_out[14], nor_1_out[15], nor_1_out[17], nor_1_out[18], nor_1_out[19], nor_1_out[20], nor_1_out[21], nor_1_out[22], nor_1_out[23], nor_1_out[24], nor_1_out[25], nor_1_out[26], nor_1_out[27], nor_1_out[28], nor_1_out[29], nor_1_out[30], nor_1_out[31], nor_1_out[16]);

  // Notes on the sheet:
  //   Comparator
  //   Alternative
endmodule

module Datapath (
  output [31:0] v0,
  output [2:0] out_2
);

  wire alu_1_zero, and_1_out, clock_1_out, controlunit_1_alusrc, controlunit_1_branch, controlunit_1_regdst,
       controlunit_1_regwrite;
  wire [2:0] bitselector_1_out, bitselector_6_out, bitselector_7_out, bitselector_8_out,
       controlunit_1_alucontrol;
  wire [3:0] bitselector_2_out, bitselector_3_out;
  wire [7:0] adder_1_out, adder_2_out, bit_extender_2_out, multiplexer_1_out, register_1_q, shifter_1_out;
  wire [10:0] bitselector_4_out;
  wire [15:0] bitselector_5_out;
  wire [31:0] alu_1_y, bit_extender_1_out, multiplexer_3_out, registerfile_1_rd1, registerfile_1_rd2,
       rom_1_data, shifter_2_out;

  Multiplexer #(.width(8)) multiplexer_1 (
    .in0(adder_1_out), .in1(adder_2_out), .out(multiplexer_1_out), .sel(and_1_out));  // open: en
  Clock clock_1 (.out(clock_1_out));
  Register register_1 (.D(multiplexer_1_out), .Q(register_1_q), .clk(clock_1_out));  // open: en, clr
  Adder adder_1 (.a(register_1_q), .b(8'h4), .out(adder_1_out));  // open: cin, cout
  Shifter #(.shift("lr")) shifter_1 (.in(register_1_q), .\dist (3'b010), .out(shifter_1_out));
  ROM #(.dataWidth(32)) rom_1 (.addr(shifter_1_out), .data(rom_1_data));  // open: sel
  BitSelector #(.width(32), .group(3)) bitselector_1 (.in(rom_1_data), .out(bitselector_1_out), .sel(4'b0111));
  BitSelector #(.width(32), .group(4)) bitselector_2 (.in(rom_1_data), .out(bitselector_2_out), .sel(3'b100));
  BitSelector #(.width(32), .group(4)) bitselector_3 (.in(rom_1_data), .out(bitselector_3_out), .sel(3'b100));
  BitSelector #(.width(32), .group(11)) bitselector_4 (.in(rom_1_data), .out(bitselector_4_out), .sel(2'b01));
  BitSelector #(.width(32), .group(16)) bitselector_5 (.in(rom_1_data), .out(bitselector_5_out), .sel(1'b0));
  BitSelector #(.width(4), .group(3)) bitselector_6 (.in(bitselector_2_out), .out(bitselector_6_out), .sel(1'b0));
  Multiplexer #(.width(3)) multiplexer_2 (
    .in0(bitselector_7_out), .in1(bitselector_8_out), .out(out_2), .sel(controlunit_1_regdst));  // open: en
  BitSelector #(.width(4), .group(3)) bitselector_7 (.in(bitselector_3_out), .out(bitselector_7_out), .sel(1'b0));
  BitSelector #(.width(11), .group(3)) bitselector_8 (.in(bitselector_4_out), .out(bitselector_8_out), .sel(2'b00));
  assign bit_extender_1_out = {{16{bitselector_5_out[15]}}, bitselector_5_out};  // Bit_Extender bit_extender_1
  and and_1 (and_1_out, alu_1_zero, controlunit_1_branch);
  ControlUnit controlunit_1 (
    .Instruction(rom_1_data), .RegDst(controlunit_1_regdst), .RegWrite(controlunit_1_regwrite),
    .ALUControl(controlunit_1_alucontrol), .Branch(controlunit_1_branch), .ALUSrc(controlunit_1_alusrc));
  RegisterFile registerfile_1 (
    .CLK(clock_1_out), .A1(bitselector_1_out), .WD3(alu_1_y), .A2(bitselector_6_out),
    .WE3(controlunit_1_regwrite), .RD1(registerfile_1_rd1), .RD2(registerfile_1_rd2), .A3(out_2), .V0(v0));
  Multiplexer #(.width(32)) multiplexer_3 (
    .in0(registerfile_1_rd2), .in1(bit_extender_1_out), .out(multiplexer_3_out), .sel(controlunit_1_alusrc));  // open: en
  Shifter #(.width(32)) shifter_2 (.in(bit_extender_1_out), .\dist (5'b00010), .out(shifter_2_out));
  Bit_Extender #(.in_width(32), .out_width(8)) bit_extender_2 (.in(shifter_2_out), .out(bit_extender_2_out));
  ALU alu_1 (
    .F(controlunit_1_alucontrol), .B(multiplexer_3_out), .A(registerfile_1_rd1), .Y(alu_1_y),
    .Zero(alu_1_zero));
  Adder adder_2 (.a(bit_extender_2_out), .b(adder_1_out), .out(adder_2_out));  // open: cin, cout

  // Notes on the sheet:
  //   PC
  //   Instruction Memory
  //   contents of rom_1 (hex, n*v repeats v):
  //   20040003 2085ffff 20860000 2084ffff 20020000 451020 20c6ffff 20010000 10260003 20 1000fffa 20
  //   2084ffff 20450000 2086ffff 20010001 10240003 20 1000fff2 20 1000ffff
  //   Control Unit
endmodule

module Tests (
  output [31:0] Y,
  output [7:0] out_2,
  output [7:0] out_3,
  output [2:0] out_4
);

  BitSelector #(.width(32), .group(8)) bitselector_1 (.in(32'h12356789), .out(out_2), .sel(2'b01));
  BitSelector #(.width(32), .group(8)) bitselector_2 (.in(32'h12356789), .out(out_3), .sel(2'b01));
  BitSelector #(.group(3)) bitselector_3 (.in(out_3), .out(out_4), .sel(2'b00));

  assign Y = 32'hf4010207;

  // Notes on the sheet:
  //   binary values in Logisim. Convince yourself how the bits are displayed.
  //   Example 2: The bit selector is configured to have 32  
  //   bit group #1 (starting at index 0) is selected for the output.
  //   That is, the 8 bits 0x67 at bit indices 15..8  are sent to the output.
  //   Example 3: Now, assume that you want to extract 3 bits at   
  //   Example 1: A simple example that illustrates how 32-bit values are displayed as 
  //   input bits and 8 output bits. The parameter constant is 1, which means that   
  //   bit indices 10..8. This can be accoplished by putting two bit selecotrs in series.
endmodule

module RegisterFile (
  input  CLK,
  input  [2:0] A1,
  input  [31:0] WD3,
  input  [2:0] A2,
  input  WE3,
  input  [2:0] A3,
  output [31:0] RD1,
  output [31:0] RD2,
  output [31:0] V0
);

  wire and_1_out, and_2_out, and_3_out, and_4_out, and_5_out, and_6_out, and_7_out, decoder_1_out0,
       decoder_1_out1, decoder_1_out2, decoder_1_out3, decoder_1_out4, decoder_1_out5, decoder_1_out6,
       decoder_1_out7;
  wire [31:0] register_1_q, register_2_q, register_4_q, register_5_q, register_6_q, register_7_q,
       register_8_q;

  Decoder #(.select(3)) decoder_1 (
    .out0(decoder_1_out0), .out1(decoder_1_out1), .out2(decoder_1_out2), .out3(decoder_1_out3),
    .out4(decoder_1_out4), .out5(decoder_1_out5), .out6(decoder_1_out6), .out7(decoder_1_out7), .sel(A3));  // open: en
  and and_1 (and_1_out, WE3, decoder_1_out1);
  and and_2 (and_2_out, WE3, decoder_1_out2);
  and and_3 (and_3_out, WE3, decoder_1_out3);
  and and_4 (and_4_out, WE3, decoder_1_out4);
  and and_5 (and_5_out, WE3, decoder_1_out5);
  and and_6 (and_6_out, WE3, decoder_1_out6);
  and and_7 (and_7_out, WE3, decoder_1_out7);
  Register #(.width(32)) register_1 (.D({32{1'b0}}), .en(decoder_1_out0), .Q(register_1_q), .clk(CLK));  // open: clr
  Register #(.width(32)) register_2 (.D(WD3), .en(and_1_out), .Q(register_2_q), .clk(CLK));  // open: clr
  Register #(.width(32)) register_3 (.D(WD3), .en(and_2_out), .Q(V0), .clk(CLK));  // open: clr
  Register #(.width(32)) register_4 (.D(WD3), .en(and_3_out), .Q(register_4_q), .clk(CLK));  // open: clr
  Register #(.width(32)) register_5 (.D(WD3), .en(and_4_out), .Q(register_5_q), .clk(CLK));  // open: clr
  Register #(.width(32)) register_6 (.D(WD3), .en(and_5_out), .Q(register_6_q), .clk(CLK));  // open: clr
  Register #(.width(32)) register_7 (.D(WD3), .en(and_6_out), .Q(register_7_q), .clk(CLK));  // open: clr
  Register #(.width(32)) register_8 (.D(WD3), .en(and_7_out), .Q(register_8_q), .clk(CLK));  // open: clr
  Multiplexer #(.select(3), .width(32)) multiplexer_1 (
    .in0(register_1_q), .in1(register_2_q), .in2(V0), .in3(register_4_q), .in4(register_5_q),
    .in5(register_6_q), .in6(register_7_q), .in7(register_8_q), .out(RD1), .sel(A1));  // open: en
  Multiplexer #(.select(3), .width(32)) multiplexer_2 (
    .in0(register_1_q), .in1(register_2_q), .in2(V0), .in3(register_4_q), .in4(register_5_q),
    .in5(register_6_q), .in6(register_7_q), .in7(register_8_q), .out(RD2), .sel(A2));  // open: en

  // Notes on the sheet:
  //   $0 måste också timeas med CLK men nu blir det att 0 skrivs över varje gång
endmodule

module ControlUnit (
  input  [31:0] Instruction,
  output RegDst,
  output RegWrite,
  output ALUSrc,
  output [2:0] ALUControl,
  output Branch
);

  wire [1:1] comparator_4_eq;
  wire [5:0] bitselector_1_out;
  wire [31:0] shifter_1_out;

  Shifter #(.width(32), .shift("lr")) shifter_1 (.in(Instruction), .\dist (5'b11010), .out(shifter_1_out));
  BitSelector #(.width(32), .group(6)) bitselector_1 (.in(shifter_1_out), .out(bitselector_1_out), .sel(3'b000));
  Comparator #(.width(6), .mode("unsigned")) comparator_1 (
    .a(bitselector_1_out), .b(6'b001000), .eq(ALUSrc));  // open: gt, lt
  Comparator #(.width(6), .mode("unsigned")) comparator_2 (
    .a(bitselector_1_out), .b({6{1'b0}}), .eq(RegDst));  // open: gt, lt
  Comparator #(.width(6), .mode("unsigned")) comparator_3 (
    .a(bitselector_1_out), .b(6'b000100), .eq(Branch));  // open: gt, lt
  Comparator #(.width(6), .mode("unsigned")) comparator_4 (
    .a(bitselector_1_out), .b(6'b011100), .eq(comparator_4_eq[1]));  // open: gt, lt
  Multiplexer #(.select(2), .width(3)) multiplexer_1 (
    .in0(3'b010), .in1(3'b110), .in2(3'b011), .out(ALUControl), .sel({comparator_4_eq[1], Branch}));  // open: in3, en
  or or_1 (RegWrite, ALUSrc, RegDst);
endmodule
